// Digital circuit ALU.dig as structural Verilog
module ALU (
  input  [15:0] Left_Hand_Bus,
  input  [15:0] Right_Hand_Bus,
  input  Carry_In,
  input  [4:0] Instruction,
  output [15:0] Result,
  output Carry_Out,
  output Signed,
  output Overflow,
  output Zero
);

  wire _74283_1_pin9, _74283_2_pin9, _74283_3_pin9, _74283_4_pin9, and_1_out, and_3_out, and_4_out,
       and_5_out, and_6_out, and_7_out, and_8_out, and_10_out, and_11_out, Arithmetic, CarryIn, LogicalShift,
       not_4_out, or_4_out, Shift, xor_3_out, xor_5_out, xor_6_out;
  wire [0:0] or_2_out;
  wire [15:0] _74283_2_pin4, and_2_out, driver_1_out, or_1_out, xor_1_out, xor_4_out;
  wire [15:15] or_3_out;

  not not_1 (LogicalShift, Instruction[2]);
  not not_2 (Shift, Instruction[3]);
  not not_3 (Arithmetic, Instruction[4]);
  and and_1 (and_1_out, LogicalShift, CarryIn);
  assign and_2_out = Left_Hand_Bus & Right_Hand_Bus;  // And and_2, 16 bits wide
  assign or_1_out = Left_Hand_Bus | Right_Hand_Bus;  // Or or_1, 16 bits wide
  assign xor_1_out = Left_Hand_Bus ^ Right_Hand_Bus;  // XOr xor_1, 16 bits wide
  and and_3 (and_3_out, Right_Hand_Bus[15], Instruction[2]);
  and and_4 (and_4_out, Instruction[1], Shift);
  and and_5 (and_5_out, Right_Hand_Bus[0], Instruction[2]);
  Driver #(.Bits(16)) driver_1 (.in(Right_Hand_Bus), .out(driver_1_out));  // open: en
  Driver #(.Bits(16)) driver_2 (.in(and_2_out), .out(driver_1_out));  // open: en
  Driver #(.Bits(16)) driver_3 (.in(or_1_out), .out(driver_1_out));  // open: en
  Driver #(.Bits(16)) driver_4 (.in(xor_1_out), .out(driver_1_out));  // open: en
  or or_2 (or_2_out[0], and_3_out, and_1_out);
  and and_6 (and_6_out, Right_Hand_Bus[15], and_4_out);
  and and_7 (and_7_out, not_4_out, Shift);
  not not_4 (not_4_out, Instruction[1]);
  and and_8 (and_8_out, and_7_out, Right_Hand_Bus[0]);
  or or_3 (or_3_out[15], and_5_out, and_1_out);
  and and_9 (CarryIn, Carry_In, Instruction[0]);
  // XOr xor_2 has open pins: In_1=driver_1_out[0], In_2=Instruction[2], out=open
  or or_4 (or_4_out, and_6_out, and_8_out);
  assign Result = and_4_out ? {Right_Hand_Bus[14:0], or_2_out[0]} : 16'bz;  // Driver driver_5
  and and_10 (and_10_out, or_4_out, LogicalShift);
  assign Result = and_7_out ? {or_3_out[15], Right_Hand_Bus[15:1]} : 16'bz;  // Driver driver_6
  xor xor_3 (xor_3_out, CarryIn, Instruction[1]);
  assign xor_4_out = Right_Hand_Bus ^ {16{Instruction[1]}};  // XOr xor_4, 16 bits wide
  _74283 _74283_1 (
    .pin1(_74283_2_pin4[1]), .pin2(xor_4_out[1]), .pin3(Left_Hand_Bus[1]), .pin4(_74283_2_pin4[0]),
    .pin5(Left_Hand_Bus[0]), .pin6(xor_4_out[0]), .pin7(xor_3_out), .pin8(1'b0), .pin9(_74283_1_pin9),
    .pin10(_74283_2_pin4[3]), .pin11(xor_4_out[3]), .pin12(Left_Hand_Bus[3]), .pin13(_74283_2_pin4[2]),
    .pin14(Left_Hand_Bus[2]), .pin15(xor_4_out[2]), .pin16(1'b1));
  _74283 _74283_2 (
    .pin1(_74283_2_pin4[5]), .pin2(xor_4_out[5]), .pin3(Left_Hand_Bus[5]), .pin4(_74283_2_pin4[4]),
    .pin5(Left_Hand_Bus[4]), .pin6(xor_4_out[4]), .pin7(_74283_1_pin9), .pin8(1'b0), .pin9(_74283_2_pin9),
    .pin10(_74283_2_pin4[7]), .pin11(xor_4_out[7]), .pin12(Left_Hand_Bus[7]), .pin13(_74283_2_pin4[6]),
    .pin14(Left_Hand_Bus[6]), .pin15(xor_4_out[6]), .pin16(1'b1));
  _74283 _74283_3 (
    .pin1(_74283_2_pin4[9]), .pin2(xor_4_out[9]), .pin3(Left_Hand_Bus[9]), .pin4(_74283_2_pin4[8]),
    .pin5(Left_Hand_Bus[8]), .pin6(xor_4_out[8]), .pin7(_74283_2_pin9), .pin8(1'b0), .pin9(_74283_3_pin9),
    .pin10(_74283_2_pin4[11]), .pin11(xor_4_out[11]), .pin12(Left_Hand_Bus[11]), .pin13(_74283_2_pin4[10]),
    .pin14(Left_Hand_Bus[10]), .pin15(xor_4_out[10]), .pin16(1'b1));
  _74283 _74283_4 (
    .pin1(_74283_2_pin4[13]), .pin2(xor_4_out[13]), .pin3(Left_Hand_Bus[13]), .pin4(_74283_2_pin4[12]),
    .pin5(Left_Hand_Bus[12]), .pin6(xor_4_out[12]), .pin7(_74283_3_pin9), .pin8(1'b0), .pin9(_74283_4_pin9),
    .pin10(_74283_2_pin4[15]), .pin11(xor_4_out[15]), .pin12(Left_Hand_Bus[15]), .pin13(_74283_2_pin4[14]),
    .pin14(Left_Hand_Bus[14]), .pin15(xor_4_out[14]), .pin16(1'b1));
  and and_11 (and_11_out, _74283_4_pin9, Arithmetic);
  or or_5 (Carry_Out, and_11_out, and_10_out);
  assign Result = Arithmetic ? _74283_2_pin4 : 16'bz;  // Driver driver_7
  nor nor_1 (Zero, Result[7], Result[6], Result[5], Result[4], Result[3], Result[2], Result[1], Result[0], Result[8], Result[9], Result[10], Result[11], Result[12], Result[13], Result[14], Result[15]);
  xor xor_5 (xor_5_out, Left_Hand_Bus[15], Result[15]);
  xor xor_6 (xor_6_out, Result[15], Right_Hand_Bus[15]);
  and and_12 (Overflow, xor_5_out, xor_6_out);
  // Pins of 1 and 16 bits meet at driver_1_out
  // Pins of 1 and 16 bits meet at {16{Instruction[2]}}

  assign Signed = Result[15];

  // Other names for the same wires on the sheet: BitwiseMode1 = Instruction[0]; UseCarry = Instruction[0];
  //   BitwiseMode2 = Instruction[1]; Direction = Instruction[1]; Subtract = Instruction[1]; Not = Instruction[2];
  //   Rotate = Instruction[2]; Bitwise = Instruction[3]; Logical = Instruction[4]; LHSign = Left_Hand_Bus[15];
  //   RHSign = Right_Hand_Bus[15]

  // Notes on the sheet:
  //   Left_Hand_Bus: Left hand input of operation.
  //   Ignored for logical shift operations
  //   Right_Hand_Bus: Right hand input of operations.
  //   Used for logical shift operations
  //   Result: Result of the operation
  //   Carry_Out: Carry flag from the most recent operation.
  //   Carry flag is set from the following operations:
  //   Add
  //   Subract
  //   Shift
  //   Signed: Flag if the result is signed. Set by all operations
  //   (Might want to take off the and/or/etc from setting this
  //   Zero: Zero flag. Set by all operations if the result is Zero
  //   Instruction: Bit 5 will say arithmetic if off, logical if on
  //   If Bit 5 off (Arithmetic Mode)
  //   	Bit 4 & 3 ignored
  //   	Bit 2 Subtract mode if on
  //   	Bit 1 Uses carry
  //   If Bit 5 on (logic mode), bit 4 does bitwise if off, shift if on
  //   	If Bit 4 off (bitwise mode)
  //   		Bit 3 Nots result
  //   		Bits 2 & 1 determine function to use
  //   			00 - Unchanged
  //   			01 - And
  //   			10 - Or
  //   			11 - Xor
  //   	If Bit 4 on (shift mode)
  //   		Bit 3 does logical shift if off, rotate if on
  //   		Bit 2 does Direction (right off, left on)
  //   		Bit 1 does Use Carry (ignored for rot)
  //   TODO: Setup the bitwise mode selection
  //   Ensure logic modes only output when they are supposed to
  //   Get sign bit of inputs
endmodule
