// Digital circuit main.dig as structural Verilog
module main (
  input  [15:0] Bus,
  input  OE,
  input  Load,
  input  Crement,
  input  RCIi,
  input  Reset,
  input  CLK,
  input  Manual,
  input  EI,
  input  EO,
  input  BRO,
  input  [15:0] Bus_2,
  input  Manual_2,
  input  Carry_Bit,
  input  SIO1,
  input  SIO2,
  input  SIO3,
  input  SI1,
  input  SI2,
  input  SI3,
  input  SPR,
  input  ROi,
  input  RIi
);

  wire alu_1_p10, alu_1_p11, alu_1_p12, alu_1_p13, Register_Controller_p7, Register_Controller_p9,
       Register_Controller_p11, Register_Controller_p13, Register_Controller_p20, Register_Controller_p21,
       undriven, undriven_2, undriven_3, undriven_4, undriven_5, undriven_6, undriven_7, undriven_8,
       undriven_9, undriven_10, undriven_11, undriven_12, undriven_13, xor_1_out, xor_2_out;
  wire [2:1] Register_Controller_p4;
  wire [15:0] driver_1_out, registermodule_1_lho, registermodule_1_rho, registermodule_8_rho;

  LED led_1 (.in(driver_1_out[13]));
  LED led_2 (.in(driver_1_out[14]));
  LED led_3 (.in(driver_1_out[15]));
  LED led_4 (.in(driver_1_out[15]));
  LED led_5 (.in(driver_1_out[9]));
  LED led_6 (.in(driver_1_out[10]));
  LED led_7 (.in(driver_1_out[11]));
  LED led_8 (.in(driver_1_out[12]));
  LED led_9 (.in(driver_1_out[11]));
  LED led_10 (.in(driver_1_out[12]));
  LED led_11 (.in(driver_1_out[13]));
  LED led_12 (.in(driver_1_out[14]));
  LED led_13 (.in(driver_1_out[5]));
  LED led_14 (.in(driver_1_out[6]));
  LED led_15 (.in(driver_1_out[7]));
  LED led_16 (.in(driver_1_out[8]));
  LED led_17 (.in(driver_1_out[7]));
  LED led_18 (.in(driver_1_out[8]));
  LED led_19 (.in(driver_1_out[9]));
  LED led_20 (.in(driver_1_out[10]));
  LED led_21 (.in(driver_1_out[1]));
  LED led_22 (.in(driver_1_out[2]));
  LED led_23 (.in(driver_1_out[3]));
  LED led_24 (.in(driver_1_out[4]));
  LED led_25 (.in(driver_1_out[3]));
  LED led_26 (.in(driver_1_out[4]));
  LED led_27 (.in(driver_1_out[5]));
  LED led_28 (.in(driver_1_out[6]));
  LED led_29 (.in(driver_1_out[0]));
  assign driver_1_out = Manual_2 ? Bus_2 : 16'bz;  // Driver driver_1
  LED led_30 (.in(driver_1_out[0]));
  LED led_31 (.in(driver_1_out[1]));
  LED led_32 (.in(driver_1_out[2]));
  assign driver_1_out = Manual ? Bus : 16'bz;  // Driver driver_2
  LED led_33 (.in(registermodule_1_lho[15]));
  LED led_34 (.in(registermodule_1_rho[15]));
  LED led_35 (.in(registermodule_1_lho[11]));
  LED led_36 (.in(registermodule_1_lho[12]));
  LED led_37 (.in(registermodule_1_lho[13]));
  LED led_38 (.in(registermodule_1_lho[14]));
  LED led_39 (.in(registermodule_1_rho[11]));
  LED led_40 (.in(registermodule_1_rho[12]));
  LED led_41 (.in(registermodule_1_rho[13]));
  LED led_42 (.in(registermodule_1_rho[14]));
  LED led_43 (.in(registermodule_1_lho[7]));
  LED led_44 (.in(registermodule_1_lho[8]));
  LED led_45 (.in(registermodule_1_lho[9]));
  LED led_46 (.in(registermodule_1_lho[10]));
  LED led_47 (.in(registermodule_1_rho[7]));
  LED led_48 (.in(registermodule_1_rho[8]));
  LED led_49 (.in(registermodule_1_rho[9]));
  LED led_50 (.in(registermodule_1_rho[10]));
  LED led_51 (.in(registermodule_1_lho[3]));
  LED led_52 (.in(registermodule_1_lho[4]));
  LED led_53 (.in(registermodule_1_lho[5]));
  LED led_54 (.in(registermodule_1_lho[6]));
  LED led_55 (.in(registermodule_1_rho[3]));
  LED led_56 (.in(registermodule_1_rho[4]));
  LED led_57 (.in(registermodule_1_rho[5]));
  LED led_58 (.in(registermodule_1_rho[6]));
  RegisterModule registermodule_1 (
    .LHOEi(undriven_5), .RHOEi(undriven_6), .LHO(registermodule_1_lho), .RHO(registermodule_1_rho),
    .IN(driver_1_out), .CLK(CLK), .INC(Register_Controller_p4[1]), .DEC(Register_Controller_p4[2]),
    .Reset(Reset), .Load(Load), .Enablei(Register_Controller_p13));
  RegisterModule registermodule_2 (
    .LHOEi(undriven_3), .RHOEi(undriven_4), .LHO(registermodule_1_lho), .RHO(registermodule_1_rho),
    .IN(driver_1_out), .CLK(CLK), .INC(Register_Controller_p4[1]), .DEC(Register_Controller_p4[2]),
    .Reset(Reset), .Load(Load), .Enablei(Register_Controller_p11));
  RegisterModule registermodule_3 (
    .LHOEi(Register_Controller_p21), .RHOEi(undriven_2), .LHO(registermodule_1_lho),
    .RHO(registermodule_1_rho), .IN(driver_1_out), .CLK(CLK), .INC(Register_Controller_p4[1]),
    .DEC(Register_Controller_p4[2]), .Reset(Reset), .Load(Load), .Enablei(Register_Controller_p9));
  RegisterModule registermodule_4 (
    .LHOEi(Register_Controller_p20), .RHOEi(undriven), .LHO(registermodule_1_lho),
    .RHO(registermodule_1_rho), .IN(driver_1_out), .CLK(CLK), .INC(Register_Controller_p4[1]),
    .DEC(Register_Controller_p4[2]), .Reset(Reset), .Load(Load), .Enablei(Register_Controller_p7));
  LED led_59 (.in(registermodule_1_lho[0]));
  LED led_60 (.in(registermodule_1_lho[1]));
  LED led_61 (.in(registermodule_1_lho[2]));
  LED led_62 (.in(registermodule_1_rho[0]));
  LED led_63 (.in(registermodule_1_rho[1]));
  LED led_64 (.in(registermodule_1_rho[2]));
  // ALU alu_1: pin names not known; wires that end beside it: driver_1_out[4:0], EI, Carry_Bit, CLK, registermodule_1_lho, registermodule_1_rho, driver_1_out, EO, BRO, alu_1_p10, alu_1_p11, alu_1_p12, alu_1_p13
  // RegisterController Register_Controller: pin names not known; wires that end beside it: OE, Register_Controller_p4[2], driver_1_out, Register_Controller_p4[1], CLK, Reset, Register_Controller_p7, Crement, Register_Controller_p9, RCIi, Register_Controller_p11, SPR, Register_Controller_p13, SIO1, SIO2, SIO3, SI1, SI2, SI3, Register_Controller_p20, Register_Controller_p21
  LED led_65 (.in(alu_1_p10));
  LED led_66 (.in(alu_1_p11));
  LED led_67 (.in(alu_1_p11));
  LED led_68 (.in(alu_1_p12));
  LED led_69 (.in(alu_1_p13));
  RegisterModule registermodule_5 (
    .LHOEi(1'b1), .RHOEi(undriven_13), .RHO(driver_1_out), .IN(driver_1_out), .CLK(CLK),
    .INC(Register_Controller_p4[1]), .DEC(Register_Controller_p4[2]), .Reset(Reset), .Load(Load),
    .Enablei(undriven_12));  // open: LHO
  RegisterModule registermodule_6 (
    .LHOEi(1'b1), .RHOEi(undriven_11), .RHO(driver_1_out), .IN(driver_1_out), .CLK(CLK),
    .INC(Register_Controller_p4[1]), .DEC(Register_Controller_p4[2]), .Reset(Reset), .Load(Load),
    .Enablei(undriven_10));  // open: LHO
  RegisterModule registermodule_7 (
    .LHOEi(1'b1), .RHOEi(undriven_9), .RHO(driver_1_out), .IN(driver_1_out), .CLK(CLK),
    .INC(Register_Controller_p4[1]), .DEC(Register_Controller_p4[2]), .Reset(Reset), .Load(Load),
    .Enablei(undriven_8));  // open: LHO
  RegisterModule registermodule_8 (
    .LHOEi(1'b1), .RHOEi(1'b0), .RHO(registermodule_8_rho), .IN(driver_1_out), .CLK(CLK),
    .INC(Register_Controller_p4[1]), .DEC(Register_Controller_p4[2]), .Reset(Reset), .Load(Load),
    .Enablei(undriven_7));  // open: LHO
  xor xor_1 (xor_1_out, 1'b0, registermodule_8_rho[15]);
  xor xor_2 (xor_2_out, registermodule_8_rho[15], 1'b1);
  RAMSinglePortSel #(.AddrBits(15), .Bits(16)) _2_CY7C199_s (
    .A(registermodule_8_rho[14:0]), .CS(~xor_2_out), .WE(~RIi), .OE(~ROi), .D(driver_1_out));
  EEPROM #(.AddrBits(15), .Bits(16)) _2_AT28C256_s (
    .A(registermodule_8_rho[14:0]), .CS(~xor_1_out), .WE(~1'b1), .OE(~ROi), .D(driver_1_out));

  // Notes on the sheet:
  //   RCIi: default 1
  //   Manual: Manually put data on bus
  //   Manual_2: Manually put data on bus
  //   SIO1: SPR Index Out 1
  //   SIO2: SPR Index Out 1
  //   SIO3: SPR Index Out 1
  //   SI1: SPR Index Enable 1
  //   SI2: SPR Index Enable 1
  //   SI3: SPR Index Enable 1
  //   SPR: SPR enable instead of GPR
  //   ROi: RAM Out inverted, default 1
  //   RIi: RAM In inverted, default 1
  //   Main Bus
  //   Left Hand Bus
  //   Right Hand Bus
  //   Register Control Bus
  //   Memory
endmodule
