// Logisim project NOS.circ as structural Verilog: 21 circuits, main circuit main
module main (
  input  [15:0] DataBus_Write,
  input  in_2,
  input  Manual
);

  wire button_1_out, clock_1_out, controlled_buffer_1_out, not_1_out;
  wire [15:0] controlled_buffer_3_out;

  Button button_1 (.out(button_1_out));
  Clock clock_1 (.out(clock_1_out));
  not not_1 (not_1_out, Manual);
  assign controlled_buffer_1_out = not_1_out ? clock_1_out : 1'bz;  // Controlled_Buffer controlled_buffer_1
  assign controlled_buffer_1_out = Manual ? button_1_out : 1'bz;  // Controlled_Buffer controlled_buffer_2
  HCT139_2to4LineDecoder hct139_2to4linedecoder_1 ();  // open: B1, G2i, A2, B2, G1i, A1, Y12, Y13, Y20, Y21, Y22, Y23, Y10, Y11
  HCT138_3to8LineDecoder hct138_3to8linedecoder_1 ();  // open: A0, A1, A2, E3, E2i, E3i, Y0i, Y1i, Y2i, Y3i, Y4i, Y5i, Y6i, Y7i
  assign controlled_buffer_3_out = in_2 ? DataBus_Write : 16'bz;  // Controlled_Buffer controlled_buffer_3
  Pull_Resistor pull_resistor_1 (.node(controlled_buffer_3_out));
  // Probe on controlled_buffer_3_out
endmodule

module HCT138_3to8LineDecoder (
  input  A0,
  input  A1,
  input  A2,
  input  E3,
  input  E2i,
  input  E3i,
  output Y0i,
  output Y1i,
  output Y2i,
  output Y3i,
  output Y4i,
  output Y5i,
  output Y6i,
  output Y7i
);

  wire nand_1_out, nand_2_out, nand_3_out, nand_4_out, nand_5_out, nand_6_out, nand_7_out, nand_8_out,
       nand_9_out, not_1_out, not_2_out, not_3_out, not_4_out, not_5_out;

  not not_1 (not_1_out, A0);
  not not_2 (not_2_out, A1);
  not not_3 (not_3_out, A2);
  not not_4 (not_4_out, E2i);
  not not_5 (not_5_out, E3i);
  nand nand_1 (nand_1_out, E3, not_4_out, not_5_out);
  nand nand_2 (nand_2_out, not_1_out, not_2_out, not_3_out);
  nand nand_3 (nand_3_out, A0, not_2_out, not_3_out);
  nand nand_4 (nand_4_out, not_1_out, A1, not_3_out);
  nand nand_5 (nand_5_out, A0, A1, not_3_out);
  nand nand_6 (nand_6_out, not_1_out, not_2_out, A2);
  nand nand_7 (nand_7_out, A0, not_2_out, A2);
  nand nand_8 (nand_8_out, not_1_out, A1, A2);
  nand nand_9 (nand_9_out, A0, A1, A2);
  nand nand_10 (Y0i, ~nand_2_out, ~nand_1_out);  // NAND_Gate
  nand nand_11 (Y1i, ~nand_3_out, ~nand_1_out);  // NAND_Gate
  nand nand_12 (Y2i, ~nand_4_out, ~nand_1_out);  // NAND_Gate
  nand nand_13 (Y3i, ~nand_5_out, ~nand_1_out);  // NAND_Gate
  nand nand_14 (Y4i, ~nand_6_out, ~nand_1_out);  // NAND_Gate
  nand nand_15 (Y5i, ~nand_7_out, ~nand_1_out);  // NAND_Gate
  nand nand_16 (Y6i, ~nand_8_out, ~nand_1_out);  // NAND_Gate
  nand nand_17 (Y7i, ~nand_9_out, ~nand_1_out);  // NAND_Gate

  // Notes on the sheet:
  //   74HCT138
endmodule

module HCT139_2to4LineDecoder (
  input  G1i,
  input  A1,
  input  B1,
  input  G2i,
  input  A2,
  input  B2,
  output Y10,
  output Y11,
  output Y12,
  output Y13,
  output Y20,
  output Y21,
  output Y22,
  output Y23
);

  wire not_1_out, not_2_out, not_3_out, not_4_out, not_5_out, not_6_out, not_7_out, not_8_out;

  not not_1 (not_1_out, G1i);
  not not_2 (not_2_out, A1);
  not not_3 (not_3_out, A1);
  not not_4 (not_4_out, B1);
  not not_5 (not_5_out, G2i);
  not not_6 (not_6_out, A2);
  not not_7 (not_7_out, A2);
  not not_8 (not_8_out, B2);
  nand nand_1 (Y10, not_1_out, not_2_out, not_4_out);
  nand nand_2 (Y11, not_1_out, A1, not_4_out);
  nand nand_3 (Y12, not_1_out, not_3_out, B1);
  nand nand_4 (Y13, not_1_out, A1, B1);
  nand nand_5 (Y20, not_5_out, not_6_out, not_8_out);
  nand nand_6 (Y21, not_5_out, A2, not_8_out);
  nand nand_7 (Y22, not_5_out, not_7_out, B2);
  nand nand_8 (Y23, not_5_out, A2, B2);
endmodule

module HC153_4To1MultiPlexer (
  input  E1i,
  input  D13,
  input  D12,
  input  D11,
  input  D10,
  input  S0,
  input  S1,
  input  D23,
  input  D22,
  input  D21,
  input  D20,
  input  E2i,
  output Y1,
  output Y2
);

  wire and_1_out, and_2_out, and_3_out, and_4_out, and_5_out, and_6_out, and_7_out, and_8_out, not_1_out,
       not_2_out, not_3_out, not_4_out, not_5_out, not_6_out;

  not not_1 (not_1_out, E1i);
  and and_1 (and_1_out, not_1_out, not_5_out, not_3_out, D13);
  and and_2 (and_2_out, not_1_out, not_2_out, not_5_out, D12);
  or or_1 (Y1, and_1_out, and_2_out, and_3_out, and_4_out);
  and and_3 (and_3_out, not_1_out, not_3_out, not_4_out, D11);
  and and_4 (and_4_out, not_1_out, not_2_out, not_4_out, D10);
  not not_2 (not_2_out, S0);
  not not_3 (not_3_out, not_2_out);
  not not_4 (not_4_out, S1);
  not not_5 (not_5_out, not_4_out);
  and and_5 (and_5_out, D23, not_3_out, not_5_out, not_6_out);
  and and_6 (and_6_out, D22, not_2_out, not_5_out, not_6_out);
  and and_7 (and_7_out, D21, not_4_out, not_3_out, not_6_out);
  or or_2 (Y2, and_5_out, and_6_out, and_7_out, and_8_out);
  not not_6 (not_6_out, E2i);
  and and_8 (and_8_out, D20, not_2_out, not_4_out, not_6_out);
endmodule

module HCT157_SelctorMultiplexer (
  input  [3:0] A,
  input  [3:0] B,
  input  S,
  input  Ei,
  output [3:0] Y
);

  wire not_1_out;

  Multiplexer #(.enable("true"), .width(4)) multiplexer_1 (.in0(A), .in1(B), .out(Y), .sel(S), .en(not_1_out));
  not not_1 (not_1_out, Ei);
endmodule

module HCT173_QuadDTypeFF (
  input  OEi,
  input  [3:0] D,
  input  WEi,
  input  Clk,
  input  MR,
  output [3:0] Q
);

  wire not_1_out, not_2_out;
  wire [3:0] register_1_q;

  Register #(.width(4)) register_1 (.D(D), .en(not_2_out), .clk(Clk), .Q(register_1_q), .clr(MR));
  not not_1 (not_1_out, OEi);
  not not_2 (not_2_out, WEi);
  assign Q = not_1_out ? register_1_q : 4'bz;  // Controlled_Buffer controlled_buffer_1
endmodule

module HCT193_UpDownCounter (
  input  P0,
  input  P1,
  input  P2,
  input  P3,
  input  PLi,
  input  CPUi,
  input  CPDi,
  input  MR,
  output TCUi,
  output TCDi,
  output Q0,
  output Q1,
  output Q2,
  output Q3
);

  wire and_1_out, and_2_out, and_3_out, and_4_out, and_5_out, and_6_out, nand_1_out, nand_2_out, nand_3_out,
       nand_4_out, nand_5_out, nand_6_out, nand_7_out, nand_8_out, nor_1_out, nor_2_out, nor_3_out,
       nor_4_out, not_1_out, not_2_out, not_3_out, not_4_out, not_5_out, not_6_out, not_7_out, not_8_out,
       or_1_out, or_2_out, or_3_out, or_4_out, t_ff_1_qn, t_ff_2_qn, t_ff_3_qn, t_ff_4_qn;

  not not_1 (not_1_out, PLi);
  not not_2 (not_2_out, CPUi);
  not not_3 (not_3_out, CPDi);
  not not_4 (not_4_out, MR);
  nand nand_1 (nand_1_out, not_1_out, not_4_out, P0);
  not not_5 (not_5_out, nand_1_out);
  T_Flip_Flop t_ff_1 (.T(nor_1_out), .clk(nor_1_out), .Q(Q0), .Qn(t_ff_1_qn), .reset(or_1_out), .preset(not_5_out));
  nor nor_1 (nor_1_out, not_2_out, not_3_out);
  or or_1 (or_1_out, ~not_4_out, ~nand_2_out);  // OR_Gate
  nand nand_2 (nand_2_out, nand_1_out, not_1_out);
  and and_1 (and_1_out, not_2_out, Q0);
  and and_2 (and_2_out, t_ff_1_qn, not_3_out);
  nand nand_3 (nand_3_out, not_1_out, not_4_out, P1);
  not not_6 (not_6_out, nand_3_out);
  T_Flip_Flop t_ff_2 (.T(nor_2_out), .clk(nor_2_out), .Q(Q1), .Qn(t_ff_2_qn), .reset(or_2_out), .preset(not_6_out));
  nor nor_2 (nor_2_out, and_1_out, and_2_out);
  or or_2 (or_2_out, ~not_4_out, ~nand_4_out);  // OR_Gate
  nand nand_4 (nand_4_out, nand_3_out, not_1_out);
  and and_3 (and_3_out, not_2_out, Q0, Q1);
  nor nor_3 (nor_3_out, and_3_out, and_4_out);
  and and_4 (and_4_out, t_ff_2_qn, t_ff_1_qn, not_3_out);
  nand nand_5 (nand_5_out, not_1_out, not_4_out, P2);
  nand nand_6 (nand_6_out, nand_5_out, not_1_out);
  not not_7 (not_7_out, nand_5_out);
  T_Flip_Flop t_ff_3 (.T(nor_3_out), .clk(nor_3_out), .Q(Q2), .Qn(t_ff_3_qn), .reset(or_3_out), .preset(not_7_out));
  or or_3 (or_3_out, ~not_4_out, ~nand_6_out);  // OR_Gate
  and and_5 (and_5_out, not_2_out, Q1, Q0, Q2);
  and and_6 (and_6_out, t_ff_3_qn, t_ff_2_qn, t_ff_1_qn, not_3_out);
  T_Flip_Flop t_ff_4 (.T(nor_4_out), .clk(nor_4_out), .Q(Q3), .Qn(t_ff_4_qn), .reset(or_4_out), .preset(not_8_out));
  nor nor_4 (nor_4_out, and_5_out, and_6_out);
  nand nand_7 (nand_7_out, not_1_out, not_4_out, P3);
  nand nand_8 (nand_8_out, nand_7_out, not_1_out);
  not not_8 (not_8_out, nand_7_out);
  or or_4 (or_4_out, ~not_4_out, ~nand_8_out);  // OR_Gate
  nand nand_9 (TCUi, not_2_out, Q2, Q1, Q0, Q3);
  nand nand_10 (TCDi, not_3_out, t_ff_1_qn, t_ff_2_qn, t_ff_3_qn, t_ff_4_qn);

  // Notes on the sheet:
  //   PLi - Asynchronous Parallel Load Enable (inverted)
  //   MR - Master Reset
  //   CPUi - Clock Pulse Count Up (inverted)
  //   CPDi = Clock Pulse Count Down (inverted)
  //   TCUi - Terminal Carry Up (inverted) - <Carry>
  //   TCDi - Terminal Count Down (inverted) - <Borrow>
  //   CPUi - Clock Pulse Count Up (inverted)
  //   CPDi = Clock Pulse Count Down (inverted)
endmodule

module HCT283_Adder (
  input  CIn,
  input  [3:0] A,
  input  [3:0] B,
  output [3:0] S,
  output COut
);

  Adder #(.width(4)) adder_1 (.a(A), .b(B), .out(S), .cin(CIn), .cout(COut));
endmodule

module HCT574_OctalLatch (
  input  OEi,
  input  [7:0] D,
  input  CP,
  output [7:0] Q
);

  wire not_1_out;
  wire [7:0] register_1_q;

  Register register_1 (.D(D), .en(1'b1), .clk(CP), .Q(register_1_q), .clr(1'b0));
  not not_1 (not_1_out, OEi);
  assign Q = not_1_out ? register_1_q : 8'bz;  // Controlled_Buffer controlled_buffer_1
endmodule

module CY7C199_SRAM (
  input  [7:0] Input,
  input  [14:0] Address,
  input  WEi,
  input  CEi,
  input  OEi,
  output [7:0] Output
);

  wire and_1_out, and_2_out, not_1_out;
  wire [7:0] ram_1_data;

  and and_1 (and_1_out, ~WEi, ~CEi);  // AND_Gate
  and and_2 (and_2_out, ~CEi, ~OEi);  // AND_Gate
  RAM #(.addrWidth(15), .asyncread("true"), .databus("bidir")) ram_1 (
    .addr(Address), .we(and_1_out), .oe(and_2_out), .clk(and_1_out), .data(ram_1_data));
  assign ram_1_data = not_1_out ? Input : 8'bz;  // Controlled_Buffer controlled_buffer_1
  not not_1 (not_1_out, and_2_out);
  assign Output = and_2_out ? ram_1_data : 8'bz;  // Controlled_Buffer controlled_buffer_2
endmodule

module RAM_Module (
  input  [15:0] Address,
  input  [7:0] DataIn,
  input  Out,
  input  Write,
  input  CLK,
  output [7:0] DataOut
);

  wire and_1_out, and_2_out, not_1_out, not_2_out, not_3_out, not_4_out, not_5_out, not_6_out, not_7_out;
  wire [7:0] controlled_buffer_1_out;

  not not_1 (not_1_out, Out);
  not not_2 (not_2_out, CLK);
  assign controlled_buffer_1_out = not_3_out ? DataIn : 8'bz;  // Controlled_Buffer controlled_buffer_1
  not not_3 (not_3_out, Out);
  assign DataOut = Out ? controlled_buffer_1_out : 8'bz;  // Controlled_Buffer controlled_buffer_2
  and and_1 (and_1_out, CLK, not_5_out);
  not not_4 (not_4_out, not_2_out);
  not not_5 (not_5_out, not_4_out);
  CY7C199_SRAM cy7c199_sram_1 (
    .WEi(not_7_out), .CEi(Address[15]), .OEi(not_1_out), .Address(Address[14:0]),
    .Input(controlled_buffer_1_out), .Output(controlled_buffer_1_out));
  CY7C199_SRAM cy7c199_sram_2 (
    .WEi(not_7_out), .CEi(not_6_out), .OEi(not_1_out), .Address(Address[14:0]),
    .Input(controlled_buffer_1_out), .Output(controlled_buffer_1_out));
  not not_6 (not_6_out, Address[15]);
  and and_2 (and_2_out, Write, and_1_out);
  not not_7 (not_7_out, and_2_out);
endmodule

module RAMInterface_Keyboard (
  input  [15:0] MARIn,
  input  [7:0] DataBusIn,
  input  Manual,
  input  DataOut,
  input  WE,
  input  CLK,
  input  WriteValue,
  input  [7:0] RAMDataOut,
  input  DecAddress,
  input  IncAddress,
  input  OutValue,
  input  TYPE_ADDRESS,
  input  BUTTON_0,
  input  BUTTON_1,
  input  BUTTON_2,
  input  BUTTON_3,
  input  BUTTON_4,
  input  BUTTON_5,
  input  BUTTON_6,
  input  BUTTON_7,
  input  BUTTON_8,
  input  BUTTON_9,
  input  BUTTON_10,
  input  BUTTON_11,
  input  BUTTON_12,
  input  BUTTON_13,
  input  BUTTON_14,
  input  BUTTON_15,
  output [15:0] RAMAddress,
  output [7:0] RAMDataIn,
  output RAMOut,
  output A3,
  output RAMWrite,
  output B3,
  output RAMClk,
  output A4,
  output C3,
  output B4,
  output D3,
  output C4,
  output E3,
  output D4,
  output F3,
  output E4,
  output G3,
  output F4,
  output G4,
  output [7:0] DataBusOut,
  output A2,
  output B2,
  output A1,
  output C2,
  output B1,
  output D2,
  output C1,
  output E2,
  output D1,
  output F2,
  output E1,
  output G2,
  output F1,
  output G1
);

  wire and_1_out, hct193_updowncounter_1_tcdi, hct193_updowncounter_1_tcui, nand_1_out, nor_1_out, not_1_out,
       not_2_out, not_3_out, not_4_out, not_5_out, not_6_out, not_7_out, not_8_out, not_9_out, not_10_out,
       not_11_out, not_12_out, not_13_out, not_14_out, not_15_out, not_16_out, not_18_out, or_1_out;
  wire [2:2] not_17_out;
  wire [3:0] controlled_buffer_5_out;
  wire [7:0] hct193_updowncounter_1_q0, hct574_octallatch_1_q, or_5_out;

  not not_1 (not_1_out, Manual);
  not not_2 (not_2_out, DecAddress);
  nor nor_1 (nor_1_out, IncAddress, not_17_out[2]);
  assign RAMDataIn = not_1_out ? DataBusIn : 8'bz;  // Controlled_Buffer controlled_buffer_1
  assign RAMDataIn = Manual ? hct574_octallatch_1_q : 8'bz;  // Controlled_Buffer controlled_buffer_2
  HEXTo7SD hexto7sd_1 (.Value(hct193_updowncounter_1_q0[3:0]), .Display({A3, B3, C3, D3, E3, F3, G3}));
  HCT193_UpDownCounter hct193_updowncounter_1 (
    .PLi(nand_1_out), .CPUi(nor_1_out), .P0(controlled_buffer_5_out[0]), .P1(controlled_buffer_5_out[1]),
    .P2(controlled_buffer_5_out[2]), .P3(controlled_buffer_5_out[3]), .CPDi(not_2_out), .MR(1'b0),
    .Q0(hct193_updowncounter_1_q0[0]), .Q1(hct193_updowncounter_1_q0[1]), .Q2(hct193_updowncounter_1_q0[2]),
    .Q3(hct193_updowncounter_1_q0[3]), .TCDi(hct193_updowncounter_1_tcdi), .TCUi(hct193_updowncounter_1_tcui));
  nand nand_1 (nand_1_out, not_3_out, and_1_out);
  not not_3 (not_3_out, not_4_out);
  not not_4 (not_4_out, not_5_out);
  not not_5 (not_5_out, and_1_out);
  and and_1 (and_1_out, not_6_out, TYPE_ADDRESS);
  HEXTo7SD hexto7sd_2 (.Value(hct193_updowncounter_1_q0[7:4]), .Display({A4, B4, C4, D4, E4, F4, G4}));
  HCT193_UpDownCounter hct193_updowncounter_2 (
    .PLi(nand_1_out), .CPUi(hct193_updowncounter_1_tcui), .P0(hct193_updowncounter_1_q0[0]),
    .P1(hct193_updowncounter_1_q0[1]), .P2(hct193_updowncounter_1_q0[2]), .P3(hct193_updowncounter_1_q0[3]),
    .CPDi(hct193_updowncounter_1_tcdi), .MR(1'b0), .Q0(hct193_updowncounter_1_q0[4]),
    .Q1(hct193_updowncounter_1_q0[5]), .Q2(hct193_updowncounter_1_q0[6]), .Q3(hct193_updowncounter_1_q0[7]));  // open: TCDi, TCUi
  not not_6 (not_6_out, not_7_out);
  not not_7 (not_7_out, not_8_out);
  not not_8 (not_8_out, not_9_out);
  not not_9 (not_9_out, not_10_out);
  not not_10 (not_10_out, not_11_out);
  not not_11 (not_11_out, or_1_out);
  or or_1 (or_1_out, BUTTON_0, BUTTON_1, BUTTON_2, BUTTON_3, BUTTON_4, BUTTON_5, BUTTON_6, BUTTON_7, BUTTON_8, BUTTON_9, BUTTON_10, BUTTON_11, BUTTON_12, BUTTON_13, BUTTON_14, BUTTON_15);
  not not_12 (not_12_out, Manual);
  assign RAMAddress = not_12_out ? MARIn : 16'bz;  // Controlled_Buffer controlled_buffer_3
  assign RAMAddress = Manual ? {{8{1'b0}}, hct193_updowncounter_1_q0} : 16'bz;  // Controlled_Buffer controlled_buffer_4
  not not_13 (not_13_out, WriteValue);
  not not_14 (not_14_out, OutValue);
  assign {controlled_buffer_5_out, or_5_out[7:4]} = not_14_out ? hct574_octallatch_1_q : 8'bz;  // Controlled_Buffer controlled_buffer_5
  assign {controlled_buffer_5_out, or_5_out[7:4]} = OutValue ? RAMDataOut : 8'bz;  // Controlled_Buffer controlled_buffer_6
  HCT574_OctalLatch hct574_octallatch_1 (.CP(not_6_out), .D(or_5_out), .OEi(1'b0), .Q(hct574_octallatch_1_q));
  or or_2 (or_5_out[3], BUTTON_8, BUTTON_9, BUTTON_10, BUTTON_11, BUTTON_12, BUTTON_13, BUTTON_14, BUTTON_15);
  not not_15 (not_15_out, not_13_out);
  not not_16 (not_16_out, not_15_out);
  not not_17 (not_17_out[2], not_16_out);
  or or_3 (or_5_out[2], BUTTON_4, BUTTON_5, BUTTON_6, BUTTON_7, BUTTON_12, BUTTON_13, BUTTON_14, BUTTON_15);
  assign {RAMClk, RAMWrite, RAMOut} = not_18_out ? {CLK, WE, DataOut} : 3'bz;  // Controlled_Buffer controlled_buffer_7
  not not_18 (not_18_out, Manual);
  assign {RAMClk, RAMWrite, RAMOut} = Manual ? {not_17_out[2], WriteValue, OutValue} : 3'bz;  // Controlled_Buffer controlled_buffer_8
  HEXTo7SD hexto7sd_3 (.Value(controlled_buffer_5_out), .Display({A2, B2, C2, D2, E2, F2, G2}));
  or or_4 (or_5_out[1], BUTTON_2, BUTTON_3, BUTTON_6, BUTTON_7, BUTTON_10, BUTTON_11, BUTTON_14, BUTTON_15);
  assign DataBusOut = RAMOut ? RAMDataOut : 8'bz;  // Controlled_Buffer controlled_buffer_9
  HEXTo7SD hexto7sd_4 (.Value(or_5_out[7:4]), .Display({A1, B1, C1, D1, E1, F1, G1}));
  or or_5 (or_5_out[0], BUTTON_1, BUTTON_3, BUTTON_5, BUTTON_7, BUTTON_9, BUTTON_11, BUTTON_13, BUTTON_15);

  // Notes on the sheet:
  //   Lower
  //   Address
  //   Will need to use more than 1 buffer for address line
  //   Upper
  //   Run these through octal buffer
  //   Delay write signal for manual clock
  //   Upper
  //   Data
  //   Lower
endmodule

module MARFirstModule (
  input  [7:0] AddressBusIn,
  input  [7:0] AddressIn,
  input  [7:0] IDIn,
  input  ADD,
  input  Reset,
  input  Clk,
  input  In8,
  input  Inc,
  input  LoadFull,
  input  ZSIn,
  input  OutI,
  input  [7:0] Out8In,
  output [7:0] IDOut,
  output ResetOut,
  output [7:0] AddressOut,
  output In8O,
  output ClkOut,
  output RC,
  output LoadFullO,
  output ZSOut,
  output [7:0] Value,
  output OutO,
  output [7:0] Out8Out
);

  wire and_1_out, and_2_out, and_3_out, and_4_out, and_6_out, hct193_updowncounter_1_tcdi,
       hct193_updowncounter_1_tcui, hct193_updowncounter_2_tcui, hct283_adder_1_cout, hct283_adder_2_cout,
       nand_1_out, nor_1_out, nor_2_out, not_1_out, not_2_out, not_3_out, not_4_out, not_5_out;
  wire [3:0] hct157_selctormultiplexer_1_y, hct157_selctormultiplexer_2_y, hct193_updowncounter_1_q0,
       hct193_updowncounter_2_q0, hct283_adder_1_s, hct283_adder_2_s;

  not not_1 (not_1_out, Clk);
  and and_1 (and_1_out, Clk, not_3_out);
  not not_2 (not_2_out, not_1_out);
  not not_3 (not_3_out, not_2_out);
  and and_2 (and_2_out, IDIn[0], and_1_out);
  and and_3 (and_3_out, and_1_out, LoadFull);
  and and_4 (and_4_out, and_2_out, In8);
  nand nand_1 (nand_1_out, Clk, Inc);
  and and_5 (ZSOut, nor_2_out, ZSIn);
  HCT283_Adder hct283_adder_1 (
    .CIn(1'b0), .A(AddressIn[3:0]), .B(hct193_updowncounter_1_q0), .S(hct283_adder_1_s),
    .COut(hct283_adder_1_cout));
  HCT283_Adder hct283_adder_2 (
    .CIn(hct283_adder_1_cout), .A(AddressIn[7:4]), .B(hct193_updowncounter_2_q0), .S(hct283_adder_2_s),
    .COut(hct283_adder_2_cout));
  and and_6 (and_6_out, hct283_adder_2_cout, ADD);
  nor nor_1 (nor_1_out, and_3_out, and_4_out);
  nor nor_2 (nor_2_out, hct193_updowncounter_1_q0[0], hct193_updowncounter_1_q0[1], hct193_updowncounter_1_q0[2], hct193_updowncounter_1_q0[3], hct193_updowncounter_2_q0[1], hct193_updowncounter_2_q0[2], hct193_updowncounter_2_q0[3], hct193_updowncounter_2_q0[0]);
  Pull_Resistor #(.pull(1)) pull_resistor_1 (.node(ZSIn));
  HCT157_SelctorMultiplexer hct157_selctormultiplexer_1 (
    .A(AddressIn[3:0]), .B(hct283_adder_1_s), .S(ADD), .Ei(1'b0), .Y(hct157_selctormultiplexer_1_y));
  HCT157_SelctorMultiplexer hct157_selctormultiplexer_2 (
    .A(AddressIn[7:4]), .B(hct283_adder_2_s), .S(ADD), .Ei(1'b0), .Y(hct157_selctormultiplexer_2_y));
  HCT193_UpDownCounter hct193_updowncounter_1 (
    .PLi(nor_1_out), .CPUi(nand_1_out), .P0(AddressOut[0]), .P1(AddressOut[1]), .P2(AddressOut[2]),
    .P3(AddressOut[3]), .CPDi(1'b1), .MR(Reset), .Q0(hct193_updowncounter_1_q0[0]),
    .Q1(hct193_updowncounter_1_q0[1]), .Q2(hct193_updowncounter_1_q0[2]), .Q3(hct193_updowncounter_1_q0[3]),
    .TCDi(hct193_updowncounter_1_tcdi), .TCUi(hct193_updowncounter_1_tcui));
  assign Out8Out = IDIn[0] ? {hct193_updowncounter_2_q0, hct193_updowncounter_1_q0} : 8'bz;  // Controlled_Buffer controlled_buffer_1
  assign Out8Out = not_5_out ? Out8In : 8'bz;  // Controlled_Buffer controlled_buffer_2
  HCT157_SelctorMultiplexer hct157_selctormultiplexer_3 (
    .A(hct157_selctormultiplexer_1_y), .B(AddressBusIn[3:0]), .S(LoadFull), .Ei(1'b0), .Y(AddressOut[3:0]));
  HCT157_SelctorMultiplexer hct157_selctormultiplexer_4 (
    .A(hct157_selctormultiplexer_2_y), .B(AddressBusIn[7:4]), .S(LoadFull), .Ei(1'b0), .Y(AddressOut[7:4]));
  HCT193_UpDownCounter hct193_updowncounter_2 (
    .PLi(nor_1_out), .CPUi(hct193_updowncounter_1_tcui), .P0(AddressOut[4]), .P1(AddressOut[5]),
    .P2(AddressOut[6]), .P3(AddressOut[7]), .CPDi(hct193_updowncounter_1_tcdi), .MR(Reset),
    .Q0(hct193_updowncounter_2_q0[0]), .Q1(hct193_updowncounter_2_q0[1]), .Q2(hct193_updowncounter_2_q0[2]),
    .Q3(hct193_updowncounter_2_q0[3]), .TCUi(hct193_updowncounter_2_tcui));  // open: TCDi
  not not_4 (not_4_out, hct193_updowncounter_2_tcui);
  DotMatrix #(.matrixcols(8), .matrixrows(1)) dotmatrix_1 (
    .col0(hct193_updowncounter_2_q0[3]), .col1(hct193_updowncounter_2_q0[2]),
    .col2(hct193_updowncounter_2_q0[1]), .col3(hct193_updowncounter_2_q0[0]),
    .col4(hct193_updowncounter_1_q0[3]), .col5(hct193_updowncounter_1_q0[2]),
    .col6(hct193_updowncounter_1_q0[1]), .col7(hct193_updowncounter_1_q0[0]));
  assign Value = OutI ? {hct193_updowncounter_2_q0, hct193_updowncounter_1_q0} : 8'bz;  // Controlled_Buffer controlled_buffer_3
  not not_5 (not_5_out, IDIn[0]);
  or or_1 (RC, and_6_out, not_4_out);

  assign ClkOut = Clk;
  assign IDOut = {IDIn[0], IDIn[7:1]};
  assign In8O = In8;
  assign LoadFullO = LoadFull;
  assign OutO = OutI;
  assign ResetOut = Reset;

  // Notes on the sheet:
  //   ZSIn: pull=up
  //   Enable Line
  //   Logisim
endmodule

module Register_Module (
  input  [15:0] Data,
  input  Load,
  input  Reset,
  input  Dec,
  input  Inc,
  input  Clk,
  input  Enable,
  input  OE,
  input  LHSE,
  input  RHSE,
  output CarryOut,
  output BorrowOut,
  output [15:0] DataOut,
  output [15:0] LHO,
  output [15:0] RHO
);

  wire and_1_out, and_2_out, and_3_out, and_4_out, button_1_out, ClkEdgei, d_ff_1_qn, d_ff_2_qn,
       hct193_updowncounter_1_tcdi, hct193_updowncounter_1_tcui, hct193_updowncounter_2_tcdi,
       hct193_updowncounter_2_tcui, hct193_updowncounter_3_tcdi, hct193_updowncounter_3_tcui,
       hct193_updowncounter_4_tcdi, hct193_updowncounter_4_tcui, nand_1_out, nand_2_out, nand_3_out,
       not_1_out, not_2_out, not_3_out, not_4_out, not_5_out, or_2_out;
  wire [15:0] hct193_updowncounter_1_q0;

  and and_1 (and_1_out, Enable, Load);
  and and_2 (and_2_out, Clk, Enable);
  and and_3 (and_3_out, Enable, OE);
  not not_1 (not_1_out, Clk);
  not not_2 (not_2_out, not_1_out);
  Button button_1 (.out(button_1_out));
  nand nand_1 (nand_1_out, Dec, and_2_out);
  nand nand_2 (nand_2_out, Inc, and_2_out);
  and and_4 (and_4_out, Clk, not_3_out);
  not not_3 (not_3_out, not_2_out);
  or or_1 (ClkEdgei, Clk, not_3_out);
  or or_2 (or_2_out, Reset, button_1_out);
  nand nand_3 (nand_3_out, and_1_out, and_4_out);
  assign LHO = LHSE ? hct193_updowncounter_1_q0 : 16'bz;  // Controlled_Buffer controlled_buffer_1
  assign RHO = RHSE ? hct193_updowncounter_1_q0 : 16'bz;  // Controlled_Buffer controlled_buffer_2
  HCT193_UpDownCounter hct193_updowncounter_1 (
    .PLi(nand_3_out), .CPUi(nand_2_out), .P0(Data[0]), .P1(Data[1]), .P2(Data[2]), .P3(Data[3]),
    .CPDi(nand_1_out), .MR(or_2_out), .Q0(hct193_updowncounter_1_q0[0]), .Q1(hct193_updowncounter_1_q0[1]),
    .Q2(hct193_updowncounter_1_q0[2]), .Q3(hct193_updowncounter_1_q0[3]), .TCDi(hct193_updowncounter_1_tcdi),
    .TCUi(hct193_updowncounter_1_tcui));
  assign DataOut = and_3_out ? hct193_updowncounter_1_q0 : 16'bz;  // Controlled_Buffer controlled_buffer_3
  HCT193_UpDownCounter hct193_updowncounter_2 (
    .PLi(nand_3_out), .CPUi(hct193_updowncounter_1_tcui), .P0(Data[4]), .P1(Data[5]), .P2(Data[6]),
    .P3(Data[7]), .CPDi(hct193_updowncounter_1_tcdi), .MR(or_2_out), .Q0(hct193_updowncounter_1_q0[4]),
    .Q1(hct193_updowncounter_1_q0[5]), .Q2(hct193_updowncounter_1_q0[6]), .Q3(hct193_updowncounter_1_q0[7]),
    .TCDi(hct193_updowncounter_2_tcdi), .TCUi(hct193_updowncounter_2_tcui));
  HCT193_UpDownCounter hct193_updowncounter_3 (
    .PLi(nand_3_out), .CPUi(hct193_updowncounter_2_tcui), .P0(Data[8]), .P1(Data[9]), .P2(Data[10]),
    .P3(Data[11]), .CPDi(hct193_updowncounter_2_tcdi), .MR(or_2_out), .Q0(hct193_updowncounter_1_q0[8]),
    .Q1(hct193_updowncounter_1_q0[9]), .Q2(hct193_updowncounter_1_q0[10]),
    .Q3(hct193_updowncounter_1_q0[11]), .TCDi(hct193_updowncounter_3_tcdi), .TCUi(hct193_updowncounter_3_tcui));
  HCT193_UpDownCounter hct193_updowncounter_4 (
    .PLi(nand_3_out), .CPUi(hct193_updowncounter_3_tcui), .P0(Data[12]), .P1(Data[13]), .P2(Data[14]),
    .P3(Data[15]), .CPDi(hct193_updowncounter_3_tcdi), .MR(or_2_out), .Q0(hct193_updowncounter_1_q0[12]),
    .Q1(hct193_updowncounter_1_q0[13]), .Q2(hct193_updowncounter_1_q0[14]),
    .Q3(hct193_updowncounter_1_q0[15]), .TCDi(hct193_updowncounter_4_tcdi), .TCUi(hct193_updowncounter_4_tcui));
  D_Flip_Flop d_ff_1 (
    .D(hct193_updowncounter_4_tcui), .clk(ClkEdgei), .Qn(d_ff_1_qn), .preset(1'b0), .reset(1'b0));  // open: Q
  D_Flip_Flop d_ff_2 (
    .D(hct193_updowncounter_4_tcdi), .clk(ClkEdgei), .Qn(d_ff_2_qn), .preset(1'b0), .reset(1'b0));  // open: Q
  not not_4 (not_4_out, d_ff_1_qn);
  not not_5 (not_5_out, d_ff_2_qn);
  Transistor transistor_1 (.in(1'b1), .out(CarryOut), .gate(not_4_out));
  Transistor transistor_2 (.in(1'b1), .out(BorrowOut), .gate(not_5_out));

  // Notes on the sheet:
  //   Bus In
  //   Main Bus Out
  //   ALU Buses Out
  //   16 Bit General Purpose Register with Increment and Decrement capabilities. Has an input connection from the main bus and an output to the main bus. Also has 2 additional outputs to either the Left or Right half of the ALU activated by LeftHandOutputEnable and RightHandOutputEnable. All other functionality only applies when the Enable line is high for a specific register. This Enable line is meant to be demultiplexed by a Register Controller to determine which register does the command. Inc, Dec, and Load all occur on a falling clock edge. Output is asynchronous
  //   N-Type, not P. BOX for Logisim ONLY
endmodule

module Register_Controller (
  input  [7:0] DataBus,
  input  CLK,
  input  RControllerIn,
  input  RIn,
  input  RReset,
  input  ROut,
  input  Crement,
  input  [7:0] RegisterBusOut,
  output Enable0i,
  output Enable1i,
  output [7:0] DataBusIn,
  output Output0i,
  output Enable2i,
  output Output1i,
  output Enable3i,
  output Output2i,
  output CLKOut,
  output Output3i,
  output Load,
  output Reset,
  output OE,
  output RHO0i,
  output RHO1i,
  output RHO2i,
  output RHO3i,
  output LHO0i,
  output Inc,
  output LHO1i,
  output Dec,
  output LHO2i,
  output LHO3i,
  output [7:0] DataBusOut
);

  wire and_1_out, and_2_out, hct139_2to4linedecoder_1_p7, hct139_2to4linedecoder_1_p8,
       hct139_2to4linedecoder_2_p7, hct139_2to4linedecoder_2_p8, not_1_out, not_2_out, not_3_out, not_4_out,
       undriven;
  wire [7:0] hct574_octallatch_1_q;

  not not_1 (not_1_out, CLK);
  not not_2 (not_2_out, not_1_out);
  not not_3 (not_3_out, not_2_out);
  HCT574_OctalLatch hct574_octallatch_1 (.CP(and_2_out), .D(DataBus), .OEi(1'b0), .Q(hct574_octallatch_1_q));
  and and_1 (and_1_out, CLK, not_3_out);
  and and_2 (and_2_out, and_1_out, RControllerIn);
  assign DataBusOut = ROut ? RegisterBusOut : 8'bz;  // Controlled_Buffer controlled_buffer_1
  // HCT139_2to4LineDecoder hct139_2to4linedecoder_1: pin names not known; wires that end beside it: Output0i, Output1i, Output2i, Output3i, Output0i, 1'b0, hct139_2to4linedecoder_1_p7, hct139_2to4linedecoder_1_p8, Enable0i, Enable1i, Enable2i, Enable3i
  // HCT139_2to4LineDecoder hct139_2to4linedecoder_2: pin names not known; wires that end beside it: 1'b0, LHO0i, LHO1i, LHO2i, LHO3i, 1'b0, hct139_2to4linedecoder_2_p7, hct139_2to4linedecoder_2_p8, RHO0i, RHO1i, RHO2i, RHO3i
  not not_4 (not_4_out, undriven);
  and and_3 (Inc, undriven, Crement);
  and and_4 (Dec, Crement, not_4_out);

  assign CLKOut = CLK;
  assign DataBusIn = DataBus;
  assign Load = RIn;
  assign OE = ROut;
  assign Reset = RReset;

  // Other names for the same wires on the sheet: RO = ROut

  // Notes on the sheet:
  //   Logisim
endmodule

module ALU (
  input  CarryIn,
  input  [7:0] LeftHandIn,
  input  EO,
  input  [7:0] RightHandIn,
  input  [7:0] Instruction,
  input  InstrIn,
  input  CLK,
  output [7:0] DataOut,
  output CarryOut,
  output BorrowOut
);

  wire and_1_out, and_2_out, and_3_out, and_5_out, and_6_out, and_7_out, and_8_out, hct283_adder_1_cout,
       nor_1_out, not_1_out, not_2_out, not_3_out, not_4_out, not_5_out, not_6_out, xor_3_out;
  wire [3:0] hct283_adder_1_s, hct283_adder_2_s;
  wire [7:0] and_4_out, controlled_buffer_1_out, controlled_buffer_4_out, hct574_octallatch_1_q, or_1_out,
       xor_1_out, xor_2_out;

  and and_1 (and_1_out, InstrIn, CLK);
  not not_1 (not_1_out, and_1_out);
  not not_2 (not_2_out, not_1_out);
  not not_3 (not_3_out, not_2_out);
  HCT574_OctalLatch hct574_octallatch_1 (.CP(and_2_out), .D(Instruction), .OEi(1'b0), .Q(hct574_octallatch_1_q));
  and and_2 (and_2_out, and_1_out, not_3_out);
  not not_4 (not_4_out, hct574_octallatch_1_q[2]);
  and and_3 (and_3_out, hct574_octallatch_1_q[1], not_4_out);
  nor nor_1 (nor_1_out, hct574_octallatch_1_q[2], hct574_octallatch_1_q[1]);
  assign and_4_out = LeftHandIn & RightHandIn;  // AND_Gate and_4, 8 bits wide
  assign controlled_buffer_1_out = nor_1_out ? and_4_out : 8'bz;  // Controlled_Buffer controlled_buffer_1
  assign or_1_out = LeftHandIn | RightHandIn;  // OR_Gate or_1, 8 bits wide
  assign xor_1_out = LeftHandIn ^ RightHandIn;  // XOR_Gate xor_1, 8 bits wide
  and and_5 (and_5_out, CarryIn, hct574_octallatch_1_q[0]);
  assign xor_2_out = RightHandIn ^ {8{hct574_octallatch_1_q[1]}};  // XOR_Gate xor_2, 8 bits wide
  not not_5 (not_5_out, hct574_octallatch_1_q[1]);
  and and_6 (and_6_out, hct574_octallatch_1_q[2], not_5_out);
  assign controlled_buffer_1_out = and_3_out ? or_1_out : 8'bz;  // Controlled_Buffer controlled_buffer_2
  assign controlled_buffer_1_out = and_6_out ? xor_1_out : 8'bz;  // Controlled_Buffer controlled_buffer_3
  xor xor_3 (xor_3_out, and_5_out, hct574_octallatch_1_q[1]);
  HCT283_Adder hct283_adder_1 (
    .CIn(xor_3_out), .A(LeftHandIn[3:0]), .B(xor_2_out[3:0]), .S(hct283_adder_1_s), .COut(hct283_adder_1_cout));
  HCT283_Adder hct283_adder_2 (
    .CIn(hct283_adder_1_cout), .A(LeftHandIn[7:4]), .B(xor_2_out[7:4]), .S(hct283_adder_2_s), .COut(CarryOut));
  assign controlled_buffer_4_out = and_7_out ? controlled_buffer_1_out : 8'bz;  // Controlled_Buffer controlled_buffer_4
  and and_7 (and_7_out, hct574_octallatch_1_q[3], hct574_octallatch_1_q[6]);
  and and_8 (and_8_out, hct574_octallatch_1_q[6], not_6_out);
  not not_6 (not_6_out, hct574_octallatch_1_q[3]);
  assign controlled_buffer_4_out = and_8_out ? {hct283_adder_2_s, hct283_adder_1_s} : 8'bz;  // Controlled_Buffer controlled_buffer_5
  assign DataOut = EO ? controlled_buffer_4_out : 8'bz;  // Controlled_Buffer controlled_buffer_6
  and and_9 (BorrowOut, controlled_buffer_4_out[7], hct574_octallatch_1_q[1]);

  // Notes on the sheet:
  //   Only 4 bits used
endmodule

module Instruction_Controller (
  input  [43:0] Decoded_Instruction,
  input  [43:0] Control_Line_Expansion,
  input  ExpansionControl,
  input  [7:0] DataBus,
  input  CLK,
  input  Reset,
  input  ESC,
  output HLT,
  output [7:0] Instruction,
  output [7:0] DataOut,
  output RCI,
  output RI,
  output RO,
  output RUC,
  output CRM,
  output BRO,
  output IID,
  output [3:0] StepOut,
  output DID,
  output IDI,
  output OUT8,
  output IN8,
  output FLOD,
  output IR,
  output ADR,
  output RSR,
  output MAR,
  output PC,
  output PCO,
  output GR,
  output GRO,
  output RMO,
  output RMI,
  output FSI,
  output SF,
  output CF,
  output LF,
  output FO,
  output DFI,
  output EO,
  output EII,
  output PSH,
  output POP,
  output IOI,
  output IOO,
  output IDO,
  output SID
);

  wire and_1_out, and_2_out, and_3_out, and_4_out, and_5_out, buffer_1_out, d_ff_1_q, d_ff_1_qn, nand_1_out,
       not_1_out, not_2_out, not_3_out, not_4_out, not_5_out, not_6_out, or_1_out, or_2_out, undriven;
  wire [43:0] or_3_out, pull_resistor_1_node, pull_resistor_2_node;
  wire [43:14] controlled_buffer_4_out;

  not not_1 (not_1_out, CLK);
  and and_1 (and_1_out, CLK, or_1_out);
  or or_1 (or_1_out, controlled_buffer_4_out[42], ESC);
  HCT574_OctalLatch hct574_octallatch_1 (.CP(and_2_out), .D(DataBus), .OEi(1'b0), .Q(Instruction));
  and and_2 (and_2_out, controlled_buffer_4_out[16], and_3_out);
  and and_3 (and_3_out, CLK, not_3_out);
  not not_2 (not_2_out, not_1_out);
  not not_3 (not_3_out, not_2_out);
  HCT193_UpDownCounter hct193_updowncounter_1 (
    .PLi(1'b1), .CPUi(not_4_out), .P0(1'b0), .P1(1'b0), .P2(1'b0), .P3(1'b0), .CPDi(1'b1), .MR(or_2_out),
    .Q0(StepOut[0]), .Q1(StepOut[1]), .Q2(StepOut[2]), .Q3(StepOut[3]));  // open: TCDi, TCUi
  not not_4 (not_4_out, and_1_out);
  not not_5 (not_5_out, or_1_out);
  D_Flip_Flop d_ff_1 (.D(d_ff_1_qn), .clk(nand_1_out), .Q(d_ff_1_q), .Qn(d_ff_1_qn), .preset(1'b0), .reset(undriven));
  nand nand_1 (nand_1_out, not_5_out, CLK);
  Pull_Resistor pull_resistor_1 (.node(pull_resistor_1_node));
  assign pull_resistor_1_node = not_6_out ? Decoded_Instruction : 44'bz;  // Controlled_Buffer controlled_buffer_1
  Pull_Resistor pull_resistor_2 (.node(pull_resistor_2_node));
  assign pull_resistor_2_node = buffer_1_out ? Control_Line_Expansion : 44'bz;  // Controlled_Buffer controlled_buffer_2
  buf buffer_1 (buffer_1_out, ExpansionControl);
  not not_6 (not_6_out, ExpansionControl);
  assign DataOut = controlled_buffer_4_out[15] ? Instruction : 8'bz;  // Controlled_Buffer controlled_buffer_3
  or or_2 (or_2_out, controlled_buffer_4_out[14], Reset);
  and and_4 (and_4_out, not_5_out, d_ff_1_q);
  and and_5 (and_5_out, not_5_out, d_ff_1_qn);
  assign or_3_out = pull_resistor_1_node | pull_resistor_2_node;  // OR_Gate or_3, 44 bits wide
  assign {controlled_buffer_4_out[43:39], RCI, RI, RO, RUC, CRM, controlled_buffer_4_out[33], IID, DID, IDI, OUT8, controlled_buffer_4_out[28], FLOD, controlled_buffer_4_out[26], ADR, RSR, controlled_buffer_4_out[23:22], PCO, controlled_buffer_4_out[20], GRO, controlled_buffer_4_out[18], RMI, controlled_buffer_4_out[16:14], FSI, SF, CF, LF, FO, DFI, EO, EII, PSH, POP, IOI, IOO, IDO, SID} = or_1_out ? or_3_out : 44'bz;  // Controlled_Buffer controlled_buffer_4
  Pull_Resistor pull_resistor_3 (.node({controlled_buffer_4_out[43:39], RCI, RI, RO, RUC, CRM, controlled_buffer_4_out[33], IID, DID, IDI, OUT8, controlled_buffer_4_out[28], FLOD, controlled_buffer_4_out[26], ADR, RSR, controlled_buffer_4_out[23:22], PCO, controlled_buffer_4_out[20], GRO, controlled_buffer_4_out[18], RMI, controlled_buffer_4_out[16:14], FSI, SF, CF, LF, FO, DFI, EO, EII, PSH, POP, IOI, IOO, IDO, SID}));
  or or_4 (HLT, controlled_buffer_4_out[43], not_5_out);
  or or_5 (BRO, controlled_buffer_4_out[33], not_5_out);
  or or_6 (IN8, controlled_buffer_4_out[28], and_4_out);
  or or_7 (IR, controlled_buffer_4_out[26], and_5_out);
  or or_8 (MAR, controlled_buffer_4_out[23], and_5_out);
  or or_9 (PC, and_5_out, controlled_buffer_4_out[22]);
  or or_10 (GR, controlled_buffer_4_out[20], and_4_out);
  or or_11 (RMO, controlled_buffer_4_out[18], and_4_out);

  // Notes on the sheet:
  //   Decoded_Instruction: pull=down
  //   Control_Line_Expansion: pull=down
  //   IRI
  //   IRO
  //   SCR
  //   HaLT
  //   DSC
  //   Disable Step Counter
  //   Register Contoller In
  //   Register In
  //   Register Out
  //   Register Use Carry
  //   in/deCReMent
  //   Bypassed Register Out
  //   Inc address register conroller ID
  //   Dec ''
  //   address register controller ID In
  //   OUTput 8 address register bits
  //   INput 8 address register bits
  //   FulLLOaD
  //   Inc Register
  //   ADd Register
  //   ReSet Register
  //   activate MAR
  //   activate Program Counter
  //   PC Out
  //   activate General purpose address Register
  //   GaR Out
  //   RaM Out
  //   RaM In
  //   IRI
  //   Instruction Register In
  //   IRO
  //   Instruction Register Out
  //   SCR
  //   Step Counter Reset
  //   Flag Selector In
  //   Set Flags
  //   Clear Flags
  //   Load Flags
  //   Flags Out
  //   Disable Flags In
  //   alu Out
  //   alu Instruction In
  //   PuSH
  //   POP
  //   I/O In
  //   I/O Out
  //   i/o ID Out
  //   Set i/o ID
endmodule

module EEPROM_Decoder (
  input  [3:0] Step,
  input  [7:0] Instruction,
  output [47:0] DecodedInst
);

  ROM #(.addrWidth(12)) EEPROM_6 (.addr({Instruction, Step}), .data(DecodedInst[47:40]));
  ROM #(.addrWidth(12)) EEPROM_5 (.addr({Instruction, Step}), .data(DecodedInst[39:32]));
  ROM #(.addrWidth(12)) EEPROM_4 (.addr({Instruction, Step}), .data(DecodedInst[31:24]));
  ROM #(.addrWidth(12)) EEPROM_3 (.addr({Instruction, Step}), .data(DecodedInst[23:16]));
  ROM #(.addrWidth(12)) EEPROM_2 (.addr({Instruction, Step}), .data(DecodedInst[15:8]));
  ROM #(.addrWidth(12)) EEPROM_1 (.addr({Instruction, Step}), .data(DecodedInst[7:0]));

  // Notes on the sheet:
  //   contents of EEPROM_6 (hex, n*v repeats v):
  //   68*c 8 15*c 8 15*c 8 15*c 8 15*c 8 15*c 8 15*c 8 15*c 8 2639*c 8 15*c 8 15*c 8 15*c 8 15*c 8 15*c 8
  //   15*c 8 15*c 8 15*c 8 15*c 8 15*c 8 15*c 8 15*c 8 15*c 8 15*c 8 15*c 8 1021*c 4 13*c
  //   contents of EEPROM_5 (hex, n*v repeats v):
  //   2 2 42 22 14*2 42 22 14*2 42 22 14*2 42 22 14*2 42 2 2 2 23 11*2 42 2 2 2 23 11*2 42 2 2 2 23 11*2
  //   42 2 2 2 23 11*2 42 2 2 2 13 11*2 42 2 2 2 13 11*2 42 2 2 2 13 11*2 42 2 2 2 13 12*2 42 20 14*2 42
  //   20 14*2 42 20 14*2 42 20 269*2 42 6 14*2 42 6 14*2 42 6 14*2 42 6 14*2 42 6 14*2 42 6 14*2 42 6 14*2
  //   42 6 14*2 42 6 14*2 42 6 14*2 42 6 14*2 42 6 14*2 42 6 14*2 42 6 14*2 42 6 14*2 42 6 14*2 42 22 14*2
  //   42 22 14*2 42 22 14*2 42 22 14*2 42 22 14*2 42 22 14*2 42 22 14*2 42 22 14*2 42 22 14*2 42 22 14*2
  //   42 22 14*2 42 22 14*2 42 22 14*2 42 22 14*2 42 22 14*2 42 22 14*2 42 22 14*2 42 22 14*2 42 22 14*2
  //   42 22 14*2 42 22 14*2 42 22 14*2 42 22 14*2 42 22 14*2 42 22 14*2 42 22 14*2 42 22 14*2 42 22 14*2
  //   42 22 14*2 42 22 14*2 42 22 14*2 42 22 15*2 42 22 14*2 42 22 14*2 42 22 14*2 42 22 14*2 42 22 14*2
  //   42 22 14*2 42 22 14*2 42 22 14*2 42 22 14*2 42 22 14*2 42 22 14*2 42 22 14*2 42 22 14*2 42 22 14*2
  //   42 22 14*2 42 22 2571*2
  //   contents of EEPROM_4 (hex, n*v repeats v):
  //   8 4 4 13*0 8 4 4 13*0 8 4 4 13*0 8 4 4 13*0 8 4 4 40 0 8 10*0 8 4 4 40 0 8 10*0 8 4 4 40 0 8 10*0 8
  //   4 4 40 0 8 10*0 8 4 4 40 0 8 10*0 8 4 4 40 0 8 10*0 8 4 4 40 0 8 10*0 8 4 4 40 0 8 10*0 8 4 4 13*0 8
  //   4 4 13*0 8 4 4 13*0 8 4 4 13*0 8 4 14*0 8 4 14*0 8 4 14*0 8 4 14*0 8 4 14*0 8 4 14*0 8 4 14*0 8 4
  //   14*0 8 4 14*0 8 4 14*0 8 4 14*0 8 4 14*0 8 4 14*0 8 4 14*0 8 4 14*0 8 4 14*0 8 4 14*0 8 4 14*0 8 4
  //   14*0 8 4 14*0 8 4 14*0 8 4 14*0 8 4 14*0 8 4 14*0 8 4 14*0 8 4 14*0 8 4 14*0 8 4 14*0 8 4 14*0 8 4
  //   14*0 8 4 14*0 8 4 14*0 8 4 14*0 8 4 14*0 8 4 14*0 8 4 14*0 8 4 14*0 8 4 14*0 8 4 14*0 8 4 14*0 8 4
  //   14*0 8 4 14*0 8 4 14*0 8 4 14*0 8 4 14*0 8 4 14*0 8 4 14*0 8 4 14*0 8 4 14*0 8 4 14*0 8 4 14*0 8 4
  //   14*0 8 4 14*0 8 4 14*0 8 4 14*0 8 4 14*0 8 4 14*0 8 4 14*0 8 4 14*0 8 4 14*0 8 4 14*0 8 4 14*0 8 4
  //   14*0 8 4 14*0 8 4 4 13*0 8 4 4 13*0 8 4 4 13*0 8 4 4 13*0 8 4 4 13*0 8 4 4 13*0 8 4 4 13*0 8 4 4
  //   13*0 8 4 4 13*0 8 4 4 13*0 8 4 4 13*0 8 4 4 13*0 8 4 4 13*0 8 4 4 13*0 8 4 4 13*0 8 4 4 13*0 8 4
  //   14*0 8 4 14*0 8 4 14*0 8 4 14*0 8 4 14*0 8 4 14*0 8 4 14*0 8 4 14*0 8 4 14*0 8 4 14*0 8 4 14*0 8 4
  //   14*0 8 4 14*0 8 4 14*0 8 4 14*0 8 4 14*0 8 4 14*0 8 4 14*0 8 4 14*0 8 4 14*0 8 4 14*0 8 4 14*0 8 4
  //   14*0 8 4 14*0 8 4 14*0 8 4 14*0 8 4 14*0 8 4 14*0 8 4 14*0 8 4 14*0 8 4 14*0 8 4 14*0 8 4 14*0 8 4
  //   14*0 8 4 14*0 8 4 14*0 8 4 14*0 8 4 14*0 8 4 14*0 8 4 14*0 8 4 14*0 8 4 14*0 8 4 14*0 8 4 14*0 8 4
  //   14*0 8 4 14*0 8 4 14*0 8 4 14*0 8 4 14*0 8 4 14*0 8 4 14*0 8 4 14*0 8 4 14*0 8 4 14*0 8 4 14*0 8 4
  //   14*0 8 4 14*0 8 4 14*0 8 4 14*0 8 4 14*0 8 4 14*0 8 4 14*0 8 4 14*0 8 4 14*0 8 4 14*0 8 4 14*0 8 4
  //   14*0 8 4 14*0 8 4 14*0 8 4 14*0 8 4 14*0 8 4 14*0 8 4 14*0 8 4 14*0 8 4 14*0 8 4 14*0 8 4 14*0 8 4
  //   14*0 8 4 14*0 8 4 14*0 8 4 4 40 0 8 10*0 8 4 4 40 0 8 10*0 8 4 4 40 0 8 10*0 8 4 4 40 0 8 10*0 8 4 4
  //   40 0 8 10*0 8 4 4 40 0 8 10*0 8 4 4 40 0 8 10*0 8 4 4 40 0 8 10*0 8 4 4 40 0 8 10*0 8 4 4 40 0 8
  //   10*0 8 4 4 40 0 8 10*0 8 4 4 40 0 8 10*0 8 4 4 40 0 8 10*0 8 4 4 40 0 8 10*0 8 4 4 40 0 8 10*0 8 4 4
  //   40 0 8 10*0 8 4 14*0 8 4 14*0 8 4 14*0 8 4 14*0 8 4 14*0 8 4 14*0 8 4 14*0 8 4 14*0 8 4 14*0 8 4
  //   14*0 8 4 14*0 8 4 14*0 8 4 14*0 8 4 14*0 8 4 14*0 8 4 14*0 8 4 14*0 8 4 14*0 8 4 14*0 8 4 14*0 8 4
  //   14*0 8 4 14*0 8 4 14*0 8 4 14*0 8 4 14*0 8 4 14*0 8 4 14*0 8 4 14*0 8 4 14*0 8 4 14*0 8 4 14*0 8 4
  //   14*0 8 4 14*0 8 4 14*0 8 4 14*0 8 4 14*0 8 4 14*0 8 4 14*0 8 4 14*0 8 4 14*0 8 4 14*0 8 4 14*0 8 4
  //   14*0 8 4 14*0 8 4 14*0 8 4 14*0 8 4 14*0 8 4 14*0 8 4 14*0 8 4 14*0 8 4 14*0 8 4 14*0 8 4 14*0 8 4
  //   14*0 8 4 14*0 8 4 14*0 8 4 14*0 8 4 14*0 8 4 14*0 8 4 14*0 8 4 14*0 8 4 14*0 8 4 14*0 8 4
  //   contents of EEPROM_3 (hex, n*v repeats v):
  //   a0 45 c0 4 12*0 a0 45 c0 4 12*0 a0 45 c0 4 12*0 a0 45 c0 4 12*0 a0 45 c0 14 0 88 14 9*0 a0 45 c0 14
  //   0 88 14 9*0 a0 45 c0 14 0 88 14 9*0 a0 45 c0 14 0 88 14 9*0 a0 45 c0 14 0 88 12 9*0 a0 45 c0 14 0 88
  //   12 9*0 a0 45 c0 14 0 88 12 9*0 a0 45 c0 14 0 88 12 9*0 a0 45 c0 4 12*0 a0 45 c0 4 12*0 a0 45 c0 4
  //   12*0 a0 45 c0 4 12*0 a0 45 14*0 a0 45 14*0 a0 45 14*0 a0 45 14*0 a0 45 14*0 a0 45 14*0 a0 45 14*0 a0
  //   45 14*0 a0 45 14*0 a0 45 14*0 a0 45 14*0 a0 45 14*0 a0 45 14*0 a0 45 14*0 a0 45 14*0 a0 45 14*0 a0
  //   45 14*0 a0 45 14*0 a0 45 14*0 a0 45 14*0 a0 45 14*0 a0 45 14*0 a0 45 14*0 a0 45 14*0 a0 45 14*0 a0
  //   45 14*0 a0 45 14*0 a0 45 14*0 a0 45 14*0 a0 45 14*0 a0 45 14*0 a0 45 14*0 a0 45 14*0 a0 45 14*0 a0
  //   45 14*0 a0 45 14*0 a0 45 14*0 a0 45 14*0 a0 45 14*0 a0 45 14*0 a0 45 14*0 a0 45 14*0 a0 45 14*0 a0
  //   45 14*0 a0 45 14*0 a0 45 14*0 a0 45 14*0 a0 45 14*0 a0 45 14*0 a0 45 14*0 a0 45 14*0 a0 45 14*0 a0
  //   45 14*0 a0 45 14*0 a0 45 14*0 a0 45 14*0 a0 45 14*0 a0 45 14*0 a0 45 14*0 a0 45 14*0 a0 45 14*0 a0
  //   45 14*0 a0 45 14*0 a0 45 14*0 a0 45 c0 4 12*0 a0 45 c0 4 12*0 a0 45 c0 4 12*0 a0 45 c0 4 12*0 a0 45
  //   c0 4 12*0 a0 45 c0 4 12*0 a0 45 c0 4 12*0 a0 45 c0 4 12*0 a0 45 c0 4 12*0 a0 45 c0 4 12*0 a0 45 c0 4
  //   12*0 a0 45 c0 4 12*0 a0 45 c0 4 12*0 a0 45 c0 4 12*0 a0 45 c0 4 12*0 a0 45 c0 4 12*0 a0 45 14*0 a0
  //   45 14*0 a0 45 14*0 a0 45 14*0 a0 45 14*0 a0 45 14*0 a0 45 14*0 a0 45 14*0 a0 45 14*0 a0 45 14*0 a0
  //   45 14*0 a0 45 14*0 a0 45 14*0 a0 45 14*0 a0 45 14*0 a0 45 14*0 a0 45 14*0 a0 45 14*0 a0 45 14*0 a0
  //   45 14*0 a0 45 14*0 a0 45 14*0 a0 45 14*0 a0 45 14*0 a0 45 14*0 a0 45 14*0 a0 45 14*0 a0 45 14*0 a0
  //   45 14*0 a0 45 14*0 a0 45 14*0 a0 45 14*0 a0 45 14*0 a0 45 14*0 a0 45 14*0 a0 45 14*0 a0 45 14*0 a0
  //   45 14*0 a0 45 14*0 a0 45 14*0 a0 45 14*0 a0 45 14*0 a0 45 14*0 a0 45 14*0 a0 45 14*0 a0 45 14*0 a0
  //   45 14*0 a0 45 14*0 a0 45 14*0 a0 45 14*0 a0 45 14*0 a0 45 14*0 a0 45 14*0 a0 45 14*0 a0 45 14*0 a0
  //   45 14*0 a0 45 14*0 a0 45 14*0 a0 45 14*0 a0 45 14*0 a0 45 14*0 a0 45 14*0 a0 45 14*0 a0 45 14*0 a0
  //   45 14*0 a0 45 14*0 a0 45 14*0 a0 45 14*0 a0 45 14*0 a0 45 14*0 a0 45 14*0 a0 45 14*0 a0 45 14*0 a0
  //   45 14*0 a0 45 14*0 a0 45 14*0 a0 45 14*0 a0 45 14*0 a0 45 14*0 a0 45 14*0 a0 45 80 14 0 48 10*0 a0
  //   45 80 14 0 48 10*0 a0 45 80 14 0 48 10*0 a0 45 80 14 0 48 10*0 a0 45 80 14 0 48 10*0 a0 45 80 14 0
  //   48 10*0 a0 45 80 14 0 48 10*0 a0 45 80 14 0 48 10*0 a0 45 80 14 0 48 10*0 a0 45 80 14 0 48 10*0 a0
  //   45 80 14 0 48 10*0 a0 45 80 14 0 48 10*0 a0 45 80 14 0 48 10*0 a0 45 80 14 0 48 10*0 a0 45 80 14 0
  //   48 10*0 a0 45 80 14 0 48 10*0 a0 45 14*0 a0 45 14*0 a0 45 14*0 a0 45 14*0 a0 45 14*0 a0 45 14*0 a0
  //   45 14*0 a0 45 14*0 a0 45 14*0 a0 45 14*0 a0 45 14*0 a0 45 14*0 a0 45 14*0 a0 45 14*0 a0 45 14*0 a0
  //   45 14*0 a0 45 14*0 a0 45 14*0 a0 45 14*0 a0 45 14*0 a0 45 14*0 a0 45 14*0 a0 45 14*0 a0 45 14*0 a0
  //   45 14*0 a0 45 14*0 a0 45 14*0 a0 45 14*0 a0 45 14*0 a0 45 14*0 a0 45 14*0 a0 45 14*0 a0 45 14*0 a0
  //   45 14*0 a0 45 14*0 a0 45 14*0 a0 45 14*0 a0 45 14*0 a0 45 14*0 a0 45 14*0 a0 45 14*0 a0 45 14*0 a0
  //   45 14*0 a0 45 14*0 a0 45 14*0 a0 45 14*0 a0 45 14*0 a0 45 14*0 a0 45 14*0 a0 45 14*0 a0 45 14*0 a0
  //   45 14*0 a0 45 14*0 a0 45 14*0 a0 45 14*0 a0 45 14*0 a0 45 14*0 a0 45 14*0 a0 45 14*0 a0 45 14*0 a0
  //   45 14*0 a0 45 14*0 a0 45 14*0 a0 45
  //   contents of EEPROM_2 (hex, n*v repeats v):
  //   0 0 80 0 40 13*0 80 0 40 13*0 80 0 40 13*0 80 0 40 13*0 80 4*0 40 10*0 80 4*0 40 10*0 80 4*0 40 10*0
  //   80 4*0 40 10*0 80 4*0 40 10*0 80 4*0 40 10*0 80 4*0 40 10*0 80 4*0 40 13*0 40 15*0 40 15*0 40 15*0
  //   40 268*0 80 0 40 13*0 80 0 40 13*0 80 0 40 13*0 80 0 40 13*0 80 0 40 13*0 80 0 40 13*0 80 0 40 13*0
  //   80 0 40 13*0 80 0 40 13*0 80 0 40 13*0 80 0 40 13*0 80 0 40 13*0 80 0 40 13*0 80 0 40 13*0 80 0 40
  //   13*0 80 0 40 13*0 80 0 40 13*0 80 0 40 13*0 80 0 40 13*0 80 0 40 13*0 80 0 40 13*0 80 0 40 13*0 80 0
  //   40 13*0 80 0 40 13*0 80 0 40 13*0 80 0 40 13*0 80 0 40 13*0 80 0 40 13*0 80 0 40 13*0 80 0 40 13*0
  //   80 0 40 13*0 80 0 40 13*0 80 0 40 13*0 80 0 40 13*0 80 0 40 13*0 80 0 40 13*0 80 0 40 13*0 80 0 40
  //   13*0 80 0 40 13*0 80 0 40 13*0 80 0 40 13*0 80 0 40 13*0 80 0 40 13*0 80 0 40 13*0 80 0 40 13*0 80 0
  //   40 13*0 80 0 40 13*0 80 0 40 13*0 80 0 0 40 12*0 80 0 0 40 12*0 80 0 0 40 12*0 80 0 0 40 12*0 80 0 0
  //   40 12*0 80 0 0 40 12*0 80 0 0 40 12*0 80 0 0 40 12*0 80 0 0 40 12*0 80 0 0 40 12*0 80 0 0 40 12*0 80
  //   0 0 40 12*0 80 0 0 40 12*0 80 0 0 40 12*0 80 0 0 40 12*0 80 0 0 40 1296*0 40 15*0 40 15*0 40 15*0 40
  //   15*0 40 15*0 40 15*0 40 15*0 40 15*0 40 15*0 40 15*0 40 15*0 40 15*0 40 15*0 40 15*0 40 15*0 40
  //   contents of EEPROM_1 (hex, n*v repeats v):
  //   770*0 40 80 14*0 40 80 14*0 40 80 14*0 40 80 14*0 40 80 14*0 40 80 14*0 40 80 14*0 40 80 14*0 40 80
  //   14*0 40 80 14*0 40 80 14*0 40 80 14*0 40 80 14*0 40 80 14*0 40 80 14*0 40 80 14*0 40 80 14*0 40 80
  //   14*0 40 80 14*0 40 80 14*0 40 80 14*0 40 80 14*0 40 80 14*0 40 80 14*0 40 80 14*0 40 80 14*0 40 80
  //   14*0 40 80 14*0 40 80 14*0 40 80 14*0 40 80 14*0 40 80 14*0 40 0 80 13*0 40 0 80 13*0 40 0 80 13*0
  //   40 0 80 13*0 40 0 80 13*0 40 0 80 13*0 40 0 80 13*0 40 0 80 13*0 40 0 80 13*0 40 0 80 13*0 40 0 80
  //   13*0 40 0 80 13*0 40 0 80 13*0 40 0 80 13*0 40 0 80 13*0 40 0 80
endmodule

module ManualControl (
  input  Manual_Mode,
  input  HLT,
  input  RCI,
  input  RI,
  input  RO,
  input  RUC,
  input  CRM,
  input  SFT,
  input  ROT,
  input  NOTc,
  input  BRO,
  input  IID,
  input  DID,
  input  IDI,
  input  OUT8,
  input  IN8,
  input  FLOD,
  input  IR,
  input  ADR,
  input  RSR,
  input  MAR,
  input  PC,
  input  PCO,
  input  GR,
  input  GRO,
  input  RMO,
  input  RMI,
  input  IRI,
  input  IRO,
  input  SCR,
  input  FSI,
  input  SF,
  input  CF,
  input  LF,
  input  FO,
  input  DFI,
  input  EO,
  input  EII,
  input  PSH,
  input  POP,
  input  IOI,
  input  IOO,
  input  IDO,
  input  SID,
  output Manual_Mode_Out,
  output [43:0] out_46
);

  assign out_46 = 44'hc0200000000 ^ {HLT, 1'b0, RCI, RI, RO, RUC, CRM, SFT, ROT, NOTc, BRO, IID, DID, IDI, OUT8, IN8, FLOD, IR, ADR, RSR, MAR, PC, PCO, GR, GRO, RMO, RMI, IRI, IRO, SCR, FSI, SF, CF, LF, FO, DFI, EO, EII, PSH, POP, IOI, IOO, IDO, SID};  // XOR_Gate xor_1, 44 bits wide

  assign Manual_Mode_Out = Manual_Mode;

  // Notes on the sheet:
  //   Active Low
endmodule

module HEXTo7SD (
  input  [3:0] Value,
  output [6:0] Display
);

  wire and_1_out, and_2_out, and_3_out, and_4_out, and_5_out, and_6_out, and_7_out, and_8_out, and_9_out,
       and_10_out, and_11_out, and_12_out, and_13_out, and_14_out, and_15_out, and_16_out, and_17_out,
       and_18_out, and_19_out, and_20_out, and_21_out, and_22_out, and_23_out, and_24_out, and_25_out,
       and_26_out, and_27_out, and_28_out, and_29_out, and_30_out, and_31_out, and_32_out, and_33_out,
       and_34_out, and_35_out, and_36_out, and_37_out, and_38_out, and_39_out, and_40_out, and_41_out,
       and_42_out, and_43_out, and_44_out, and_45_out, and_46_out, and_47_out, not_1_out, not_2_out,
       not_3_out, not_4_out, or_1_out, or_2_out, or_3_out, or_4_out, or_5_out, or_6_out, or_7_out, or_8_out,
       or_9_out, or_10_out, or_12_out, or_13_out, or_14_out, or_15_out, or_16_out, or_17_out, or_18_out,
       or_20_out, or_21_out, or_22_out, or_23_out;

  not not_1 (not_1_out, Value[3]);
  not not_2 (not_2_out, Value[2]);
  not not_3 (not_3_out, Value[1]);
  not not_4 (not_4_out, Value[0]);
  and and_1 (and_1_out, Value[3], not_2_out);
  and and_2 (and_2_out, not_1_out, not_3_out);
  and and_3 (and_3_out, not_1_out, not_3_out);
  and and_4 (and_4_out, not_1_out, Value[0]);
  and and_5 (and_5_out, not_1_out, not_2_out);
  and and_6 (and_6_out, not_2_out, Value[1]);
  and and_7 (and_7_out, not_2_out, not_4_out);
  and and_8 (and_8_out, Value[1], not_4_out);
  and and_9 (and_9_out, Value[3], Value[1]);
  and and_10 (and_10_out, Value[3], Value[2]);
  and and_11 (and_11_out, not_1_out, Value[2]);
  and and_12 (and_12_out, not_2_out, Value[1]);
  and and_13 (and_13_out, Value[1], not_4_out);
  and and_14 (and_14_out, not_1_out, Value[2]);
  and and_15 (and_15_out, not_2_out, not_4_out);
  and and_16 (and_16_out, not_1_out, Value[1]);
  and and_17 (and_17_out, not_1_out, Value[2]);
  and and_18 (and_18_out, Value[2], Value[1]);
  and and_19 (and_19_out, and_1_out, not_3_out);
  and and_20 (and_20_out, not_1_out, not_2_out);
  and and_21 (and_21_out, and_2_out, not_4_out);
  and and_22 (and_22_out, not_1_out, Value[1]);
  and and_23 (and_23_out, Value[3], not_3_out);
  or or_1 (or_1_out, and_3_out, and_4_out);
  and and_24 (and_24_out, not_3_out, Value[0]);
  and and_25 (and_25_out, not_1_out, Value[2]);
  and and_26 (and_26_out, Value[3], not_2_out);
  and and_27 (and_27_out, and_5_out, not_4_out);
  and and_28 (and_28_out, and_6_out, Value[0]);
  and and_29 (and_29_out, Value[2], not_3_out);
  and and_30 (and_30_out, Value[2], Value[1]);
  and and_31 (and_31_out, Value[3], not_3_out);
  or or_2 (or_2_out, and_7_out, and_8_out);
  or or_3 (or_3_out, and_9_out, and_10_out);
  and and_32 (and_32_out, not_3_out, not_4_out);
  and and_33 (and_33_out, and_11_out, not_3_out);
  or or_4 (or_4_out, and_12_out, and_13_out);
  and and_34 (and_34_out, and_14_out, not_3_out);
  and and_35 (and_35_out, Value[3], not_2_out);
  and and_36 (and_36_out, Value[3], Value[0]);
  or or_5 (or_5_out, and_15_out, and_16_out);
  and and_37 (and_37_out, and_17_out, Value[0]);
  or or_6 (or_6_out, and_18_out, and_19_out);
  and and_38 (and_38_out, Value[3], not_4_out);
  or or_7 (or_7_out, and_20_out, and_21_out);
  and and_39 (and_39_out, not_2_out, not_4_out);
  and and_40 (and_40_out, and_22_out, Value[0]);
  and and_41 (and_41_out, and_23_out, Value[0]);
  or or_8 (or_8_out, or_1_out, and_24_out);
  or or_9 (or_9_out, and_25_out, and_26_out);
  or or_10 (or_10_out, and_27_out, and_28_out);
  and and_42 (and_42_out, and_29_out, Value[0]);
  and and_43 (and_43_out, and_30_out, not_4_out);
  and and_44 (and_44_out, and_31_out, not_4_out);
  or or_11 (Display[2], or_2_out, or_3_out);
  or or_12 (or_12_out, and_32_out, and_33_out);
  and and_45 (and_45_out, Value[2], not_4_out);
  and and_46 (and_46_out, Value[3], not_2_out);
  and and_47 (and_47_out, Value[3], Value[1]);
  or or_13 (or_13_out, or_4_out, and_34_out);
  or or_14 (or_14_out, and_35_out, and_36_out);
  or or_15 (or_15_out, or_5_out, and_37_out);
  or or_16 (or_16_out, or_6_out, and_38_out);
  or or_17 (or_17_out, or_7_out, and_39_out);
  or or_18 (or_18_out, and_40_out, and_41_out);
  or or_19 (Display[4], or_8_out, or_9_out);
  or or_20 (or_20_out, or_10_out, and_42_out);
  or or_21 (or_21_out, and_43_out, and_44_out);
  or or_22 (or_22_out, or_12_out, and_45_out);
  or or_23 (or_23_out, and_46_out, and_47_out);
  or or_24 (Display[0], or_13_out, or_14_out);
  or or_25 (Display[6], or_15_out, or_16_out);
  or or_26 (Display[5], or_17_out, or_18_out);
  or or_27 (Display[3], or_20_out, or_21_out);
  or or_28 (Display[1], or_22_out, or_23_out);

  // Notes on the sheet:
  //   47 AND Gates - 11 Chips
  //   28 OR Gates - 7 Chips
  //   4 NOT Gates - 1 Chip
  //   USE BEN EATERS
  //   THIS IS BAD
  //   19
  //   15
  //   22
  //   14
  //   2
  //   38
  //   30
  //   76
  //   60
endmodule

module NOTES (
);

  wire undriven_3, undriven_4;
  wire [3:0] hct157_selctormultiplexer_1_y, hct157_selctormultiplexer_2_y;
  wire [7:0] undriven, undriven_2;

  Controlled_Buffer controlled_buffer_1 ();  // open: in, out, en
  Controlled_Inverter controlled_inverter_1 ();  // open: in, out, en
  // NOT_Gate not_1 is placed but not wired
  // AND_Gate and_1 is placed but not wired
  // OR_Gate or_1 is placed but not wired
  HCT157_SelctorMultiplexer hct157_selctormultiplexer_1 (
    .A(undriven[3:0]), .B(undriven_2[3:0]), .S(undriven_3), .Ei(undriven_4), .Y(hct157_selctormultiplexer_1_y));
  HCT157_SelctorMultiplexer hct157_selctormultiplexer_2 (
    .A(undriven[7:4]), .B(undriven_2[7:4]), .S(undriven_3), .Ei(undriven_4), .Y(hct157_selctormultiplexer_2_y));

  // Notes on the sheet:
  //   All             are 74hc245 
  //   All              are 74hct240 
  //   All             are 74hct04 
  //   All              are 74hct08 
  //   All              are 74hct32 
  //   This gotta go FAAAST
endmodule
